# Fritzing sketch MIDI_LibValidator (saved by Fritzing 0.7.7b)
breadboards: 1

parts:
  Arduino1 = Arduino
  LCD1 = LCD screen
  LED1 = LED - 5mm [color="Red (633nm)" package="5 mm [THT]"]
  LED2 = LED - 5mm [color="Green (555nm)" package="5 mm [THT]"]
  R2 = Resistor [tolerance=±5% resistance=1k package=THT]
  R4 = Trimmer Potentiometer [maximum_resistance=10kΩ package=THT]
  R5 = Resistor [tolerance=±5% resistance=1k package=THT]
  R6 = Resistor [tolerance=±5% resistance=1k package=THT]

nets:
  N1: Arduino1.D13, LCD1.E
  N2: Arduino1.D12, LCD1.RS
  N3: Arduino1.D11, LCD1.DB7
  N4: Arduino1.D10, LCD1.DB6
  N5: Arduino1.D9, LCD1.DB5
  N6: Arduino1.D8, LCD1.DB4
  N7: Arduino1.D3, Arduino1.D2
  N8: Arduino1.D1TX, Arduino1.D0RX
  +5V: Arduino1.+5V, LCD1.VDD, LED1.cathode, LED2.cathode, R4.leg2, R5.Pin_0
  GND: Arduino1.GND, LCD1.VSS, LCD1.R/W, LCD1.LED-, R4.leg1
  N9: Arduino1.A4, R2.Pin_0
  N10: Arduino1.A5, R6.Pin_0
  N11: LCD1.V0, R4.wiper
  N12: LCD1.LED+, R5.Pin_1
  N13: LED1.anode, R6.Pin_1
  N14: LED2.anode, R2.Pin_1
